# Fritzing sketch diagrama (saved by Fritzing 0.9.6b)

parts:
  Part1 = Arduino Uno (Rev3)
  Part2 = Arduino Uno (Rev3)
  Part3 = KY-004 Key Switch Module [package="Breakout board"]
  Part4 = KY-004 Key Switch Module [package="Breakout board"]
  LED1 = LED - 5mm [color="Red (633nm)" current=0.030 package="5 mm [THT]"]

nets:
  N1: Part1.D4, Part3.S
  N2: Part1.D5_PWM, Part4.S
  N3: Part2.GND, LED1.cathode
  N4: Part2.D4, LED1.anode
  VIN: Part3.Vin, Part4.Vin
  N5: Part3.-, Part4.-

notes:
  MAESTRO
  ESCLAVO

custom parts:
  KY-004 Key Switch Module: Arduino Key Switch Module Keyes KY-004 is a push button that will output a high signal when pressed.
